# Fritzing sketch AR07_2LED (saved by Fritzing 0.9.3b)
breadboards: 1

parts:
  부품1 = Arduino Uno (Rev3)
  R1 = Resistor [tolerance=±10% resistance=220 package=THT]
  R2 = Resistor [tolerance=±10% resistance=220 package=THT]
  LED1 = LED - 5mm [color="Red (633nm)" package="5 mm [THT]"]
  LED2 = LED - 5mm [color="Green (555nm)" package="5 mm [THT]"]

nets:
  N1: 부품1.D3_PWM, LED1.anode
  N2: 부품1.D5_PWM, LED2.anode
  N3: 부품1.GND, R1.Pin_1, R2.Pin_1
  N4: R1.Pin_0, LED2.cathode
  N5: R2.Pin_0, LED1.cathode
