# Fritzing sketch ARnn_4led (saved by Fritzing 0.9.3b)
breadboards: 1

parts:
  부품2 = Arduino Uno (Rev3)
  R3 = Resistor [tolerance=±10% resistance=220 package=THT]
  R4 = Resistor [tolerance=±10% resistance=220 package=THT]
  LED3 = LED - 5mm [color="Green (555nm)" package="5 mm [THT]"]
  LED4 = LED - 5mm [color="Red (633nm)" package="5 mm [THT]"]
  R5 = Resistor [tolerance=±10% resistance=220 package=THT]
  R6 = Resistor [tolerance=±10% resistance=220 package=THT]  # not connected
  LED5 = LED - 5mm [color="Blue (470nm)" package="5 mm [THT]"]
  LED6 = LED - 5mm [color="Yellow (592nm)" package="5 mm [THT]"]
  R7 = Resistor [tolerance=±10% resistance=220 package=THT]

nets:
  N1: 부품2.D9_PWM, LED6.anode
  N2: 부품2.D3_PWM, LED4.anode
  N3: 부품2.D5_PWM, LED3.anode
  N4: 부품2.D6_PWM, LED5.anode
  N5: 부품2.GND, R3.Pin_1, R4.Pin_1, R7.Pin_1
  N6: R3.Pin_0, LED4.cathode
  N7: R4.Pin_0, LED3.cathode
  N8: R5.Pin_0, LED5.cathode
  N9: LED6.cathode, R7.Pin_0
